# Fritzing sketch circuit (saved by Fritzing 0.9.4)
breadboards: 2

parts:
  WeMos_D1_Mini1 = WeMos D1 Mini
  Componente1 = Analog Digital MUX Breakout
  R1 = Resistor [tolerance=±5% resistance=220 package="0603 [SMD]"]
  R7 = Resistor [tolerance=±5% resistance=220 package="0603 [SMD]"]
  R8 = Resistor [tolerance=±5% resistance=220 package="0603 [SMD]"]
  R9 = Resistor [tolerance=±5% resistance=220 package="0603 [SMD]"]
  R10 = Resistor [tolerance=±5% resistance=220 package="0603 [SMD]"]
  R11 = Resistor [tolerance=±5% resistance=220 package="0603 [SMD]"]
  R12 = Resistor [tolerance=±5% resistance=220 package="0603 [SMD]"]
  R13 = Resistor [tolerance=±5% resistance=220 package="0603 [SMD]"]
  S1 = Pushbutton [package="[THT]"]
  S2 = Pushbutton [package="[THT]"]
  S3 = Pushbutton [package="[THT]"]
  S4 = Pushbutton [package="[THT]"]
  S5 = Pushbutton [package="[THT]"]
  S6 = Pushbutton [package="[THT]"]
  S7 = Pushbutton [package="[THT]"]
  S8 = Pushbutton [package="[THT]"]
  LED1 = LED - 5mm [color="Red (633nm)" package="5 mm [THT]"]
  Q1 = TRANSISTOR_NPN [package=to-92]
  IR1 = TSOP312.., 314.. [package=THT]
  Componente2 = InvenSense MPU6050

nets:
  VCC: WeMos_D1_Mini1.3V3, Componente1.VCC, S1.Pin_3, S1.Pin_4, S2.Pin_3, S2.Pin_4, S3.Pin_3, S3.Pin_4, S4.Pin_3, S4.Pin_4, S5.Pin_3, S5.Pin_4, S6.Pin_3, S6.Pin_4, S7.Pin_3, S7.Pin_4, S8.Pin_3, S8.Pin_4, LED1.anode, IR1.Data, Componente2.VCC
  N1: WeMos_D1_Mini1.D1, Q1.B
  N2: WeMos_D1_Mini1.D2, IR1.GND
  N3: WeMos_D1_Mini1.D3, Componente2.SCL
  N4: WeMos_D1_Mini1.D4, Componente2.SDA
  N5: WeMos_D1_Mini1.D5, Componente1.S1
  N6: WeMos_D1_Mini1.D6, Componente1.S2
  N7: WeMos_D1_Mini1.D7, Componente1.S3
  N8: WeMos_D1_Mini1.D8, Componente1.SIG
  GND: WeMos_D1_Mini1.G, Componente1.GND, Componente1.EN, Componente1.S0, R1.Pin_0, R7.Pin_0, R8.Pin_0, R9.Pin_0, R10.Pin_0, R11.Pin_0, R12.Pin_0, R13.Pin_0, Q1.E, IR1.Vs, Componente2.GND
  N9: R1.Pin_1, S1.Pin_1, S1.Pin_2
  N10: R7.Pin_1, S2.Pin_1, S2.Pin_2
  N11: R8.Pin_1, S3.Pin_1, S3.Pin_2
  N12: R9.Pin_1, S4.Pin_1, S4.Pin_2
  N13: R10.Pin_1, S5.Pin_1, S5.Pin_2
  N14: R11.Pin_1, S6.Pin_1, S6.Pin_2
  N15: R12.Pin_1, S8.Pin_1, S8.Pin_2
  N16: R13.Pin_1, S7.Pin_1, S7.Pin_2
  N17: LED1.cathode, Q1.C
